// Logisim project CPU.circ as structural Verilog: 14 circuits, main circuit CPU
module ALU (
  input  zx,
  input  nx,
  input  zy,
  input  ny,
  input  f,
  input  no,
  input  [15:0] x,
  input  [15:0] y,
  output zr,
  output ng,
  output [15:0] outputPin
);

  wire or_1_out;
  wire [15:0] adder_1_out, and_1_out, multiplexer_1_out, multiplexer_2_out, multiplexer_3_out,
       multiplexer_4_out, multiplexer_5_out, not_1_out, not_2_out, not_3_out;

  Multiplexer #(.width(16)) multiplexer_1 (.in0(x), .in1({16{1'b0}}), .out(multiplexer_1_out), .sel(zx));
  Multiplexer #(.width(16)) multiplexer_2 (.in0(y), .in1({16{1'b0}}), .out(multiplexer_2_out), .sel(zy));
  assign not_1_out = ~multiplexer_1_out;  // NOT_Gate not_1, 16 bits wide
  assign not_2_out = ~multiplexer_2_out;  // NOT_Gate not_2, 16 bits wide
  Multiplexer #(.width(16)) multiplexer_3 (.in0(multiplexer_1_out), .in1(not_1_out), .out(multiplexer_3_out), .sel(nx));
  Multiplexer #(.width(16)) multiplexer_4 (.in0(multiplexer_2_out), .in1(not_2_out), .out(multiplexer_4_out), .sel(ny));
  assign and_1_out = multiplexer_3_out & multiplexer_4_out;  // AND_Gate and_1, 16 bits wide
  Adder #(.width(16)) adder_1 (.a(multiplexer_3_out), .b(multiplexer_4_out), .out(adder_1_out));  // open: cin, cout
  Multiplexer #(.width(16)) multiplexer_5 (.in0(and_1_out), .in1(adder_1_out), .out(multiplexer_5_out), .sel(f));
  assign not_3_out = ~multiplexer_5_out;  // NOT_Gate not_3, 16 bits wide
  Multiplexer #(.width(16)) multiplexer_6 (
    .in0(multiplexer_5_out), .in1(not_3_out), .out({ng, outputPin[14:0]}), .sel(no));
  or or_1 (or_1_out, outputPin[0], outputPin[1], outputPin[2], outputPin[3], outputPin[4], outputPin[5], outputPin[6], outputPin[7], outputPin[8], outputPin[9], outputPin[10], outputPin[11], outputPin[12], outputPin[13], outputPin[14], ng);
  not not_4 (zr, or_1_out);

  assign outputPin[15] = ng;
endmodule

module DFlipFlop (
  input  D,
  input  clockPin,
  output Q,
  output NotQ
);

  wire nand_1_out, nand_2_out, not_1_out;

  not not_1 (not_1_out, D);
  nand nand_1 (nand_1_out, D, clockPin);
  nand nand_2 (nand_2_out, not_1_out, clockPin);
  nand nand_3 (Q, nand_1_out, NotQ);
  nand nand_4 (NotQ, Q, nand_2_out);
endmodule

module Bit (
  input  load,
  input  inputPin,
  input  clockPin,
  output outputPin
);

  wire multiplexer_1_out;

  Multiplexer multiplexer_1 (.in0(outputPin), .in1(inputPin), .out(multiplexer_1_out), .sel(load));
  DFlipFlop dflipflop_1 (.D(multiplexer_1_out), .clockPin(clockPin), .Q(outputPin));  // open: NotQ
endmodule

module BitRegister (
  input  [15:0] inputPin,
  input  load,
  input  clockPin,
  input  reset,
  output [15:0] outputPin
);

  wire [15:0] multiplexer_1_out;

  Multiplexer #(.width(16)) multiplexer_1 (.in0(outputPin), .in1(inputPin), .out(multiplexer_1_out), .sel(load));
  Register #(.width(16)) register_1 (.D(multiplexer_1_out), .clk(clockPin), .Q(outputPin), .clr(reset));  // open: en
endmodule

module RAM8 (
  input  clockPin,
  input  load,
  input  [2:0] address,
  input  [15:0] inputPin,
  output [15:0] outputPin
);

  wire demultiplexer_1_out0, demultiplexer_1_out1, demultiplexer_1_out2, demultiplexer_1_out3,
       demultiplexer_1_out4, demultiplexer_1_out5, demultiplexer_1_out6, demultiplexer_1_out7;
  wire [15:0] bitregister_1_p4, bitregister_2_p4, bitregister_3_p4, bitregister_4_p4, bitregister_5_p4,
       bitregister_6_p4, bitregister_7_p4, bitregister_8_p4;

  Demultiplexer #(.select(3), .tristate("true")) demultiplexer_1 (
    .out0(demultiplexer_1_out0), .out1(demultiplexer_1_out1), .out2(demultiplexer_1_out2),
    .out3(demultiplexer_1_out3), .out4(demultiplexer_1_out4), .out5(demultiplexer_1_out5),
    .out6(demultiplexer_1_out6), .out7(demultiplexer_1_out7), .in(load), .sel(address));
  // BitRegister bitregister_1: pin names not known; wires that end beside it: demultiplexer_1_out0, clockPin, inputPin, bitregister_1_p4
  // BitRegister bitregister_2: pin names not known; wires that end beside it: demultiplexer_1_out1, clockPin, inputPin, bitregister_2_p4
  // BitRegister bitregister_3: pin names not known; wires that end beside it: demultiplexer_1_out2, clockPin, inputPin, bitregister_3_p4
  // BitRegister bitregister_4: pin names not known; wires that end beside it: demultiplexer_1_out3, clockPin, inputPin, bitregister_4_p4
  // BitRegister bitregister_5: pin names not known; wires that end beside it: demultiplexer_1_out4, clockPin, inputPin, bitregister_5_p4
  // BitRegister bitregister_6: pin names not known; wires that end beside it: demultiplexer_1_out5, clockPin, inputPin, bitregister_6_p4
  // BitRegister bitregister_7: pin names not known; wires that end beside it: demultiplexer_1_out6, clockPin, inputPin, bitregister_7_p4
  // BitRegister bitregister_8: pin names not known; wires that end beside it: demultiplexer_1_out7, clockPin, inputPin, bitregister_8_p4
  Multiplexer #(.select(3), .width(16)) multiplexer_1 (
    .in0(bitregister_1_p4), .in1(bitregister_2_p4), .in2(bitregister_3_p4), .in3(bitregister_4_p4),
    .in4(bitregister_5_p4), .in5(bitregister_6_p4), .in6(bitregister_7_p4), .in7(bitregister_8_p4),
    .out(outputPin), .sel(address));
endmodule

module CPU (
  input  in_1,
  input  in_2,
  input  in_3,
  input  in_4,
  input  in_5,
  input  in_6,
  input  in_7,
  output [15:0] outputPin,
  output zr,
  output ng,
  output [15:0] out_11
);

  wire arithmeticinstructiontoalu_1_f, arithmeticinstructiontoalu_1_no, arithmeticinstructiontoalu_1_nx,
       arithmeticinstructiontoalu_1_ny, arithmeticinstructiontoalu_1_zx, arithmeticinstructiontoalu_1_zy,
       demultiplexer_1_out0, demultiplexer_1_out1, demultiplexer_1_out2, demultiplexer_1_out3,
       demultiplexer_1_out4, demultiplexer_1_out5, demultiplexer_1_out6, demultiplexer_1_out7,
       opcodechecker_1_ldr, opcodechecker_1_str, or_1_out, or_2_out;
  wire [8:0] opcodechecker_1_add;
  wire [14:0] programcounter_1_outputpin;
  wire [15:0] alu_1_outputpin, DataMemory_dout, InstructionMemory_data, multiplexer_2_out, multiplexer_3_out,
       multiplexer_4_out, R0_outputpin, R1_outputpin, R2_outputpin, R3_outputpin, R4_outputpin, R5_outputpin,
       R6_outputpin, registermuxsimplification_1_outputpin;

  ArithmeticInstructionToALU arithmeticinstructiontoalu_1 (
    .operations(opcodechecker_1_add), .zx(arithmeticinstructiontoalu_1_zx),
    .nx(arithmeticinstructiontoalu_1_nx), .zy(arithmeticinstructiontoalu_1_zy),
    .ny(arithmeticinstructiontoalu_1_ny), .f(arithmeticinstructiontoalu_1_f),
    .no(arithmeticinstructiontoalu_1_no));
  ProgramCounter programcounter_1 (
    .reset(in_4), .load(in_5), .increment(in_6), .clockPin(in_7), .outputPin(programcounter_1_outputpin));  // open: inputPin
  Multiplexer multiplexer_1 ();  // open: in0, in1, out, sel
  Demultiplexer #(.select(3)) demultiplexer_1 (
    .out0(demultiplexer_1_out0), .out1(demultiplexer_1_out1), .out2(demultiplexer_1_out2),
    .out3(demultiplexer_1_out3), .out4(demultiplexer_1_out4), .out5(demultiplexer_1_out5),
    .out6(demultiplexer_1_out6), .out7(demultiplexer_1_out7), .in(in_1), .sel(InstructionMemory_data[10:8]));
  ROM #(.addrWidth(15), .dataWidth(16)) InstructionMemory (
    .addr(programcounter_1_outputpin), .data(InstructionMemory_data));
  ALU alu_1 (
    .zx(arithmeticinstructiontoalu_1_zx), .nx(arithmeticinstructiontoalu_1_nx),
    .zy(arithmeticinstructiontoalu_1_zy), .ny(arithmeticinstructiontoalu_1_ny),
    .f(arithmeticinstructiontoalu_1_f), .no(arithmeticinstructiontoalu_1_no),
    .x(registermuxsimplification_1_outputpin), .y(registermuxsimplification_1_outputpin), .zr(zr), .ng(ng),
    .outputPin(alu_1_outputpin));
  Multiplexer #(.width(16)) multiplexer_2 (
    .in0(multiplexer_3_out), .in1(alu_1_outputpin), .out(multiplexer_2_out), .sel(or_1_out));
  or or_1 (or_1_out, opcodechecker_1_add[0], opcodechecker_1_add[1], opcodechecker_1_add[2], opcodechecker_1_add[3], opcodechecker_1_add[4], opcodechecker_1_add[5], opcodechecker_1_add[6], opcodechecker_1_add[7], opcodechecker_1_add[8]);
  OpCodeChecker opcodechecker_1 (
    .OpCode(InstructionMemory_data[15:11]), .ldr(opcodechecker_1_ldr), .str(opcodechecker_1_str),
    .add(opcodechecker_1_add[0]), .sub(opcodechecker_1_add[1]), .inc(opcodechecker_1_add[2]),
    .dec(opcodechecker_1_add[3]), .andcode(opcodechecker_1_add[4]), .orcode(opcodechecker_1_add[5]),
    .xorcode(opcodechecker_1_add[6]), .notcode(opcodechecker_1_add[7]), .negcode(opcodechecker_1_add[8]));  // open: dbnxt, swp, jmp, jz, endcode
  Multiplexer #(.width(16)) multiplexer_3 (
    .in0({16{1'b0}}), .in1(DataMemory_dout), .out(multiplexer_3_out), .sel(opcodechecker_1_ldr));
  Multiplexer #(.width(16)) multiplexer_4 (
    .in0({16{1'b0}}), .in1(registermuxsimplification_1_outputpin), .out(multiplexer_4_out), .sel(or_2_out));
  or or_2 (or_2_out, opcodechecker_1_ldr, opcodechecker_1_str);
  BitRegister R0 (
    .inputPin(multiplexer_2_out), .load(demultiplexer_1_out0), .clockPin(in_2), .outputPin(R0_outputpin));  // open: reset
  BitRegister R1 (
    .inputPin(multiplexer_2_out), .load(demultiplexer_1_out1), .clockPin(in_2), .outputPin(R1_outputpin));  // open: reset
  BitRegister R2 (
    .inputPin(multiplexer_2_out), .load(demultiplexer_1_out2), .clockPin(in_2), .outputPin(R2_outputpin));  // open: reset
  BitRegister R3 (
    .inputPin(multiplexer_2_out), .load(demultiplexer_1_out3), .clockPin(in_2), .outputPin(R3_outputpin));  // open: reset
  BitRegister R4 (
    .inputPin(multiplexer_2_out), .load(demultiplexer_1_out4), .clockPin(in_2), .outputPin(R4_outputpin));  // open: reset
  BitRegister R5 (
    .inputPin(multiplexer_2_out), .load(demultiplexer_1_out5), .clockPin(in_2), .outputPin(R5_outputpin));  // open: reset
  BitRegister R6 (
    .inputPin(multiplexer_2_out), .load(demultiplexer_1_out6), .clockPin(in_2), .outputPin(R6_outputpin));  // open: reset
  BitRegister R7 (
    .inputPin(multiplexer_2_out), .load(demultiplexer_1_out7), .clockPin(in_2), .outputPin(out_11));  // open: reset
  RegisterMUXSimplification registermuxsimplification_1 (
    .R0toR3({R0_outputpin, R1_outputpin, R2_outputpin, R3_outputpin}),
    .R4toR7({R4_outputpin, R5_outputpin, R6_outputpin, out_11}), .sel(InstructionMemory_data[7:5]),
    .outputPin(registermuxsimplification_1_outputpin));
  RegisterMUXSimplification registermuxsimplification_2 (
    .R0toR3({R0_outputpin, R1_outputpin, R2_outputpin, R3_outputpin}),
    .R4toR7({R4_outputpin, R5_outputpin, R6_outputpin, out_11}), .sel(InstructionMemory_data[10:8]),
    .outputPin(registermuxsimplification_1_outputpin));
  RAM #(.addrWidth(16), .dataWidth(16)) DataMemory (
    .addr(multiplexer_4_out), .we(opcodechecker_1_str), .oe(opcodechecker_1_ldr), .clk(in_3),
    .din(registermuxsimplification_1_outputpin), .dout(DataMemory_dout));

  // Notes on the sheet:
  //   contents of InstructionMemory (hex, n*v repeats v):
  //   700
endmodule

module PixelCounter (
  input  clockPin,
  input  reset,
  output [15:0] address,
  output [6:0] XOutput,
  output [6:0] YOutput
);

  wire XCounter_carry;
  wire [8:0] XCounter_q, YCounter_q;

  Counter #(.max('h7f), .width(16)) XCounter (
    .Q({XCounter_q, XOutput}), .carry(XCounter_carry), .clk(clockPin), .clr(reset));  // open: load, D, count, up
  Counter #(.max('h7f), .trigger("falling"), .width(16)) YCounter (
    .Q({YCounter_q, YOutput}), .clk(XCounter_carry), .clr(reset));  // open: load, D, count, carry, up
  Multiplier #(.width(16)) multiplier_1 (
    .a({YCounter_q, YOutput}), .b(16'h14), .out(address), .cin({XCounter_q, XOutput}));  // open: cout
endmodule

module Screen (
  input  in_1,
  input  [15:0] in_2,
  input  clockPin,
  input  reset,
  input  writeEnable
);

  wire [6:0] pixelcounter_1_xoutput, pixelcounter_1_youtput;
  wire [15:0] pixelcounter_1_address, ScreenMemory_dout;

  PixelCounter pixelcounter_1 (
    .clockPin(clockPin), .reset(reset), .address(pixelcounter_1_address), .XOutput(pixelcounter_1_xoutput),
    .YOutput(pixelcounter_1_youtput));
  RAM #(.addrWidth(16), .dataWidth(16)) ScreenMemory (
    .addr(pixelcounter_1_address), .we(in_1), .oe(in_1), .clk(clockPin), .din(in_2), .dout(ScreenMemory_dout));
  // RGB_Video #(.cursor("No Cursor"), .scale(8)) rgb_video_1: pin names not known; wires that end beside it: clockPin, writeEnable, pixelcounter_1_xoutput, pixelcounter_1_youtput, ScreenMemory_dout
endmodule

module ProgramCounter (
  input  [14:0] inputPin,
  input  reset,
  input  load,
  input  increment,
  input  clockPin,
  output [14:0] outputPin
);

  wire or_1_out, or_2_out;
  wire [14:0] adder_1_out, multiplexer_1_out, multiplexer_2_out, multiplexer_3_out, multiplexer_4_out;

  Adder #(.width(15)) adder_1 (.a(outputPin), .b(15'h1), .out(adder_1_out));  // open: cin, cout
  Multiplexer #(.width(15)) multiplexer_1 (
    .in0(outputPin), .in1(adder_1_out), .out(multiplexer_1_out), .sel(increment));
  Multiplexer #(.width(15)) multiplexer_2 (
    .in0(multiplexer_1_out), .in1(inputPin), .out(multiplexer_2_out), .sel(load));
  Multiplexer #(.width(15)) multiplexer_3 (
    .in0(multiplexer_2_out), .in1({15{1'b0}}), .out(multiplexer_3_out), .sel(reset));
  or or_1 (or_1_out, load, increment);
  or or_2 (or_2_out, or_1_out, reset);
  Multiplexer #(.width(15)) multiplexer_4 (
    .in0(outputPin), .in1(multiplexer_3_out), .out(multiplexer_4_out), .sel(or_2_out));
  Register #(.width(15)) register_1 (.D(multiplexer_4_out), .clk(clockPin), .Q(outputPin));  // open: en, clr
endmodule

module InstructionDecoder (
  input  [10:0] flags,
  input  [4:0] OpCode,
  output [2:0] out_3,
  output [15:0] AddressBus
);

  OpCodeChecker opcodechecker_1 (.OpCode(OpCode));  // open: ldr, str, dbnxt, swp, add, sub, inc, dec, andcode, orcode, xorcode, notcode, negcode, jmp, jz, endcode
  Multiplexer #(.width(16)) multiplexer_1 (.in1({16{1'b0}}), .out(AddressBus));  // open: in0, sel

  assign out_3 = flags[10:8];
endmodule

module OpCodeChecker (
  input  [4:0] OpCode,
  output ldr,
  output str,
  output dbnxt,
  output swp,
  output add,
  output sub,
  output inc,
  output dec,
  output andcode,
  output orcode,
  output xorcode,
  output notcode,
  output negcode,
  output jmp,
  output jz,
  output endcode
);

  wire comparator_16_gt;

  Comparator #(.mode("unsigned"), .width(5)) comparator_1 (.a(OpCode), .b({5{1'b0}}), .eq(ldr));  // open: gt, lt
  Comparator #(.mode("unsigned"), .width(5)) comparator_2 (.a(OpCode), .b(5'b00001), .eq(str));  // open: gt, lt
  Comparator #(.mode("unsigned"), .width(5)) comparator_3 (.a(OpCode), .b(5'b00010), .eq(dbnxt));  // open: gt, lt
  Comparator #(.mode("unsigned"), .width(5)) comparator_4 (.a(OpCode), .b(5'b00011), .eq(swp));  // open: gt, lt
  Comparator #(.mode("unsigned"), .width(5)) comparator_5 (.a(OpCode), .b(5'b00100), .eq(add));  // open: gt, lt
  Comparator #(.mode("unsigned"), .width(5)) comparator_6 (.a(OpCode), .b(5'b00101), .eq(sub));  // open: gt, lt
  Comparator #(.mode("unsigned"), .width(5)) comparator_7 (.a(OpCode), .b(5'b00110), .eq(inc));  // open: gt, lt
  Comparator #(.mode("unsigned"), .width(5)) comparator_8 (.a(OpCode), .b(5'b00111), .eq(dec));  // open: gt, lt
  Comparator #(.mode("unsigned"), .width(5)) comparator_9 (.a(OpCode), .b(5'b01000), .eq(andcode));  // open: gt, lt
  Comparator #(.mode("unsigned"), .width(5)) comparator_10 (.a(OpCode), .b(5'b01001), .eq(orcode));  // open: gt, lt
  Comparator #(.mode("unsigned"), .width(5)) comparator_11 (.a(OpCode), .b(5'b01010), .eq(xorcode));  // open: gt, lt
  Comparator #(.mode("unsigned"), .width(5)) comparator_12 (.a(OpCode), .b(5'b01011), .eq(notcode));  // open: gt, lt
  Comparator #(.mode("unsigned"), .width(5)) comparator_13 (.a(OpCode), .b(5'b01100), .eq(negcode));  // open: gt, lt
  Comparator #(.mode("unsigned"), .width(5)) comparator_14 (.a(OpCode), .b(5'b01101), .eq(jmp));  // open: gt, lt
  Comparator #(.mode("unsigned"), .width(5)) comparator_15 (.a(OpCode), .b(5'b01110), .eq(jz));  // open: gt, lt
  Comparator #(.mode("unsigned"), .width(5)) comparator_16 (
    .a(OpCode), .b(5'b01111), .gt(comparator_16_gt), .eq(endcode));  // open: lt
endmodule

module RegisterMUXSimplification (
  input  [63:0] R0toR3,
  input  [63:0] R4toR7,
  input  [2:0] sel,
  output [15:0] outputPin
);

  Multiplexer #(.select(3), .width(16)) multiplexer_1 (
    .in0(R0toR3[63:48]), .in1(R0toR3[47:32]), .in2(R0toR3[31:16]), .in3(R0toR3[15:0]), .in4(R4toR7[63:48]),
    .in5(R4toR7[47:32]), .in6(R4toR7[31:16]), .in7(R4toR7[15:0]), .out(outputPin), .sel(sel));
endmodule

module Test (
  input  [8:0] operations,
  output no
);

  or or_1 (no, operations[8], operations[7], operations[5], operations[2], operations[1]);
endmodule

module ArithmeticInstructionToALU (
  input  [8:0] operations,
  output zx,
  output nx,
  output zy,
  output ny,
  output f,
  output no
);

  or or_1 (zx, operations[8], operations[7], operations[5], operations[2], operations[1]);
  or or_2 (nx, operations[8], operations[3], operations[2], operations[1], operations[0]);
  or or_3 (zy, operations[8], operations[7], operations[5], operations[3], operations[2]);
  or or_4 (ny, operations[8], operations[7], operations[3], operations[2]);
  or or_5 (f, operations[8], operations[5], operations[3], operations[2], operations[1]);

  assign no = 1'b0;
endmodule
